# Fritzing sketch epir (saved by Fritzing 0.7.0b)
breadboards: 1

parts:
  Arduino1 = Arduino
  R1 = Resistor [tolerance=±5% resistance=10k package=THT]
  zilog_ePir = mystery part, 8 pins [chip_label="ZILOG ePIR" spacing=300mil]

nets:
  N1: Arduino1.GND, zilog_ePir.pin1, zilog_ePir.pin3, zilog_ePir.pin4
  N2: Arduino1.D2, zilog_ePir.pin5
  N3: Arduino1.3V3, R1.Pin_0, zilog_ePir.pin2
  N4: R1.Pin_1, zilog_ePir.pin6
